// Digital circuit microprocessor.dig as structural Verilog
module microprocessor (
  input  clk,
  input  [15:0] in,
  input  reset,
  output [15:0] accum
);

  wire [7:0] brainless_1_p13;
  wire [9:0] controller_1_control;
  wire [15:0] addressgen_1_addr__bus;
  wire [15:8] brainless_1_p13_2;

  addressGen addressgen_1 (
    .data__bus({brainless_1_p13_2, brainless_1_p13}), .clk(clk), .reset(reset),
    .use__pc(controller_1_control[9]), .load__mar(controller_1_control[8]), .addr__bus(addressgen_1_addr__bus));
  controller controller_1 (
    .clk(clk), .clr(reset), .data_in(brainless_1_p13), .load__ir(controller_1_control[0]),
    .control(controller_1_control));
  // brainless brainless_1: pin names not known; wires that end beside it: addressgen_1_addr__bus, in, controller_1_control[7], controller_1_control[6], controller_1_control[5], controller_1_control[4], controller_1_control[3], controller_1_control[2], controller_1_control[1], clk, reset, accum, {brainless_1_p13_2, brainless_1_p13}
endmodule
